# Fritzing sketch Receiver (saved by Fritzing 1.0.5)
breadboards: 1

parts:
  MCU1 = Raspberry Pi Zero
  M1 = fc-51 [package=THT]
  S1 = Pushbutton [package="[THT]"]
  MCU2 = Raspberry Pi Zero
  M4 = fc-51 [package=THT]

nets:
  N1: MCU1.pin_8, S1.Pin_1, S1.Pin_2
  N2: MCU1.pin_14, MCU1.pin_39, M1.pin1
  N3: MCU1.pin_35, M1.pin3
  N4: MCU1.pin_38, M1.pin2, S1.Pin_3, S1.Pin_4
  N5: MCU2.pin_26, M4.pin1
  N6: MCU2.pin_38, M4.pin2
  N7: MCU2.pin_40, M4.pin3

notes:
  IR TRANSMITTER
  VCC -> 5V
  IR RECEIVER
  VCC -> 3.3 V
  BTN -> INPUT_PULlUP
